# Fritzing sketch 2900Final_CircuitDiagram (saved by Fritzing 1.0.1rc)
breadboards: 1

parts:
  Part1 = Arduino Uno (Rev3) - ICSP
  M1 = fc-51 [package=THT]
  VCC1 = Battery block 9V
  U1 = LCD-16X2 [package=lcd-16x2]
  R1 = Rotary Potentiometer (Small) [maximum_resistance=10kΩ knob_status=50% power=0.5W package=THT]
  A1 = Dual VNH2SP30 Motor Driver [part_number=MD03A]
  M3 = Stepper Motor - Bipolar
  Part2 = RFID-RC522-v2

nets:
  N1: Part1.A2, A1.Pin_2
  N2: Part1.A3, A1.Pin_3
  N3: Part1.A4/SDA, A1.Pin_13
  N4: Part1.A5/SCL, A1.Pin_14
  N5: Part1.ICSP_MISO, Part1.D12/MISO, Part2.MISO
  N6: Part1.ICSP_MOSI, Part1.D11_PWM/MOSI, Part2.MOSI
  N7: Part1.D8, U1.DB7
  N8: Part1.D10_PWM/SS, Part2.SDA
  N9: Part1.D13/SCK, Part2.SCK
  N10: Part1.D2, M1.pin1
  N11: Part1.D3_PWM, U1.RS
  N12: Part1.D4, U1.E
  N13: Part1.D5_PWM, U1.DB4
  N14: Part1.D6_PWM, U1.DB5
  N15: Part1.D7, U1.DB6
  3V3: Part1.3V3, Part2.3.3V
  N16: M1.pin2, VCC1.-, U1.VSS, U1.R_W, U1.K, R1.leg2
  N17: M1.pin3, VCC1.+, U1.A
  N18: U1.VDD, R1.leg1
  N19: U1.VO, R1.wiper
  N20: A1.Pin_16, M3.D
  N21: A1.Pin_17, M3.B
  N22: A1.Pin_20, M3.C
  N23: A1.Pin_21, M3.A

custom parts:
  RFID-RC522-v2: A simple China made RFID-RC522 Reader; do check the pin labels, as this is a MFRC522 based clone.
